# Fritzing sketch AutomatedTemperature (saved by Fritzing 0.9.4)

parts:
  R7 = Trimmer Potentiometer [maximum_resistance=10kΩ package=THT]
  HC-SR5 = hc-sr04
  LED8 = RGB LED (com. cathode, rgb) [package="5 mm [THT]"]  # not connected
  LED9 = LED - 5mm [color="Yellow (595nm)" package="5 mm [THT]"]  # not connected
  LED10 = LED - 5mm [color="Green (565nm)" package="5 mm [THT]"]
  Arduino_Nano1 = Arduino Nano (Rev3.0)
  MLX90614_I2C_Interface1 = MLX90614 [package=to-39]
  U3 = SWITCH-SPST-2 [package=switch-spst-vertical]  # not connected
  LED11 = LED - 5mm [color="Red (633nm)" package="5 mm [THT]"]
  LCD_DISPLAY_16_x_3 = LCD screen
  Passive_Buzzer1 = Piezo Speaker  # not connected
  R8 = Resistor [tolerance=±5% resistance=220 package=THT]
  R9 = Resistor [tolerance=±5% resistance=220 package=THT]
  5v_DC_Power_Supply1 = Power plug

nets:
  N1: R7.wiper, LCD_DISPLAY_16_x_3.V0
  N2: HC-SR5.Trig, Arduino_Nano1.D12/MISO
  N3: HC-SR5.Echo, Arduino_Nano1.D11/MOSI
  GND: LED10.cathode, Arduino_Nano1.GND, LED11.cathode, 5v_DC_Power_Supply1.GND
  N4: Arduino_Nano1.D2, LCD_DISPLAY_16_x_3.RS
  N5: Arduino_Nano1.D3, LCD_DISPLAY_16_x_3.E
  N6: Arduino_Nano1.D4, LCD_DISPLAY_16_x_3.DB4
  N7: Arduino_Nano1.D5, LCD_DISPLAY_16_x_3.DB5
  N8: Arduino_Nano1.D6, LCD_DISPLAY_16_x_3.DB6
  N9: Arduino_Nano1.D7, LCD_DISPLAY_16_x_3.DB7
  N10: Arduino_Nano1.D8, R8.Pin_0
  N11: Arduino_Nano1.D9, R9.Pin_0
  VIN: Arduino_Nano1.VIN, LCD_DISPLAY_16_x_3.VDD
  5V: Arduino_Nano1.5V, 5v_DC_Power_Supply1.VCC
  N12: Arduino_Nano1.A5, MLX90614_I2C_Interface1.PWM_SDA
  N13: Arduino_Nano1.A4, MLX90614_I2C_Interface1.SCL_VZ
